# Fritzing sketch 23-08-22 lab (saved by Fritzing 0.9.6b)

parts:
  Part1 = Arduino Uno (Rev3)
  Grove1 = Grove OLED 128x96
  HC-SR04_Sensor_1 = HC-SR04 Ultrasonic Distance Sensor
  M1 = fc-51 [package=THT]

nets:
  N1: Part1.A4/SDA, Grove1.SDA
  N2: Part1.A5/SCL, Grove1.SCL
  N3: Part1.D8, M1.pin1
  N4: Part1.D12/MISO, HC-SR04_Sensor_1.ECHO
  N5: Part1.D13/SCK, HC-SR04_Sensor_1.TRIG
  VCC: Part1.5V, Grove1.VCC, HC-SR04_Sensor_1.VCC, M1.pin3
  GND: Part1.GND, Grove1.GND, HC-SR04_Sensor_1.GND, M1.pin2
